# Fritzing sketch usb-cw-adapter (saved by Fritzing 0.9.4)
circuit board: 5.4cm x 1.8cm
breadboards: 1

parts:
  Part1 = Adafruit QT Py [part_number="Adafruit #4600"]
  LED1 = LED - 3mm [color="Red (633nm)" package="3 mm [THT]"]
  LED2 = LED - 3mm [color="Red (633nm)" package="3 mm [THT]"]
  R1 = Resistor [tolerance=±5% resistance=51 package=THT]
  JP1 = Header 4 [package=screwterminal-3.5mm-4_lock]
  U1 = 3.5mm stereo jack [part_number=PJ-324M package=audio-jack]
  R2 = Resistor [tolerance=±5% resistance=51 package=THT]

nets:
  GND: Part1.GND, LED1.cathode, LED2.cathode, JP1.2, JP1.3, U1.GND
  N1: Part1.A0, U1.L-ch
  N2: Part1.A1, U1.R-ch
  N3: Part1.A2, JP1.4
  N4: Part1.A3, JP1.1
  N5: Part1.TX_A6, R1.Pin_1
  N6: Part1.RX_A7, R2.Pin_0
  N7: LED1.anode, R1.Pin_0
  N8: LED2.anode, R2.Pin_1

custom parts:
  Adafruit QT Py: What a cutie pie! Or is it... a QT Py? This diminutive dev board comes with our favorite lil chip, the SAMD21 (as made famous in our GEMMA M0 and Trinket M0 boards). This time it comes with our favorite connector - the STEMMA QT, a chainable I2C port that can be used with any of our STEMMA QT sensors and accessories. OLEDs! Inertial Measurment Units! Sensors a-plenty. All plug-and-play thanks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
  3.5mm stereo jack: Stereo audio jack with bypass switches. PJ-324M Fritzing can't do slots so the pin holes are 2off 1mm holes with a 0.1mm spacer to prevent drill breakages when put into production. If put into production the bridge section will have to be manually cut out.
